// Logisim project Lab1_Ex2.circ as structural Verilog: 1 circuit, main circuit main
module main (
  input  X1,
  input  X2,
  input  X3,
  input  Y1,
  input  Y2,
  input  Y3,
  input  X4,
  input  X5,
  input  X6,
  input  Y4,
  input  Y5,
  input  Y6,
  output Z1,
  output Z2,
  output Z3,
  output Z4,
  output Z5,
  output Z6
);

  and and_1 (Z1, X1, Y1);
  nand nand_1 (Z4, X4, Y4);
  or or_1 (Z2, X2, Y2);
  nor nor_1 (Z5, X5, Y5);
  xor xor_1 (Z3, X3, Y3);
  xnor xnor_1 (Z6, X6, Y6);

  // Notes on the sheet:
  //   Basic 2-Input AND Gate
  //   Basic 2-Input NAND Gate
  //   Basic 2-Input OR Gate
  //   Basic 2-Input NOR Gate
  //   Basic 2-Input XOR Gate
  //   Basic 2-Input NXOR Gate
endmodule
