// Logisim project Lab1_Ex3.circ as structural Verilog: 1 circuit, main circuit main
module main (
  input  X1,
  input  Y1,
  input  X2,
  input  Y2,
  input  X3,
  input  Y3,
  output Z1,
  output Z2,
  output Z3
);

  and and_1 (Z1, X1, Y1);
  or or_1 (Z2, X2, Y2);
  xor xor_1 (Z3, X3, Y3);
endmodule
