// Logisim project Lab2_Ex2.circ as structural Verilog: 1 circuit, main circuit main
module main (
  input  a,
  input  b,
  input  c_in,
  output sum,
  output c_out
);

  wire and_1_out, and_2_out, xor_1_out;

  xor xor_1 (xor_1_out, a, b);
  and and_1 (and_1_out, b, a);
  xor xor_2 (sum, xor_1_out, c_in);
  and and_2 (and_2_out, c_in, xor_1_out);
  or or_1 (c_out, and_2_out, and_1_out);

  // Notes on the sheet:
  //   1 - Bit full adder
endmodule
