// Logisim project Lab2_Ex4.circ as structural Verilog: 2 circuits, main circuit 1b_full_adder
module _1b_full_adder (
  input  a,
  input  b,
  input  c_in,
  output Sum,
  output c_out
);

  wire AND_2_out, AND_out, XOR_out;

  xor XOR (XOR_out, a, b);
  and AND (AND_out, b, a);
  and AND_2 (AND_2_out, c_in, XOR_out);
  xor XOR_2 (Sum, XOR_out, c_in);
  or OR (c_out, AND_2_out, AND_out);

  // Notes on the sheet:
  //   1-Bit full adder
endmodule

module main (
  input  [7:0] A,
  input  [7:0] B,
  output [7:0] Sum,
  output Carry_out
);

  wire n1b_full_adder_1_c_out, n1b_full_adder_2_c_out, n1b_full_adder_3_c_out, n1b_full_adder_4_c_out,
       n1b_full_adder_5_c_out, n1b_full_adder_6_c_out, n1b_full_adder_7_c_out;

  _1b_full_adder u_1b_full_adder_1 (.a(A[0]), .b(B[0]), .c_in(1'b0), .Sum(Sum[0]), .c_out(n1b_full_adder_1_c_out));
  _1b_full_adder u_1b_full_adder_2 (
    .a(A[1]), .b(B[1]), .c_in(n1b_full_adder_1_c_out), .Sum(Sum[1]), .c_out(n1b_full_adder_2_c_out));
  _1b_full_adder u_1b_full_adder_3 (
    .a(A[2]), .b(B[2]), .c_in(n1b_full_adder_2_c_out), .Sum(Sum[2]), .c_out(n1b_full_adder_3_c_out));
  _1b_full_adder u_1b_full_adder_4 (
    .a(A[3]), .b(B[3]), .c_in(n1b_full_adder_3_c_out), .Sum(Sum[3]), .c_out(n1b_full_adder_4_c_out));
  _1b_full_adder u_1b_full_adder_5 (
    .a(A[4]), .b(B[4]), .c_in(n1b_full_adder_4_c_out), .Sum(Sum[4]), .c_out(n1b_full_adder_5_c_out));
  _1b_full_adder u_1b_full_adder_6 (
    .a(A[5]), .b(B[5]), .c_in(n1b_full_adder_5_c_out), .Sum(Sum[5]), .c_out(n1b_full_adder_6_c_out));
  _1b_full_adder u_1b_full_adder_7 (
    .a(A[6]), .b(B[6]), .c_in(n1b_full_adder_6_c_out), .Sum(Sum[6]), .c_out(n1b_full_adder_7_c_out));
  _1b_full_adder u_1b_full_adder_8 (.a(A[7]), .b(B[7]), .c_in(n1b_full_adder_7_c_out), .Sum(Sum[7]), .c_out(Carry_out));
endmodule
