// Logisim project Lab3_Ex1.circ as structural Verilog: 1 circuit, main circuit main
module main (
  input  W,
  input  X,
  input  Y,
  input  Z
);

  wire and_1_out, and_2_out, and_3_out, and_4_out, and_5_out, and_6_out, and_7_out, and_8_out, not_1_out,
       not_2_out, not_3_out, not_4_out, not_5_out, not_6_out, or_1_out, or_2_out, xnor_1_out;

  not not_1 (not_1_out, Y);
  not not_2 (not_2_out, X);
  not not_3 (not_3_out, Y);
  not not_4 (not_4_out, W);
  not not_5 (not_5_out, X);
  and and_1 (and_1_out, X, not_1_out, Z);
  and and_2 (and_2_out, not_2_out, not_3_out, Z);
  and and_3 (and_3_out, not_4_out, X, Y);
  and and_4 (and_4_out, W, not_5_out, Y);
  and and_5 (and_5_out, W, X, Y);
  not not_6 (not_6_out, Y);
  or or_1 (or_1_out, and_1_out, and_2_out, and_3_out, and_4_out, and_5_out);
  and and_6 (and_6_out, not_6_out, Z);
  and and_7 (and_7_out, Y, X);
  and and_8 (and_8_out, Y, W);
  or or_2 (or_2_out, and_6_out, and_7_out, and_8_out);
  xnor xnor_1 (xnor_1_out, or_1_out, or_2_out);
  LED led_1 (.in(xnor_1_out));
endmodule
