// Logisim project Lab3_Ex2.circ as structural Verilog: 1 circuit, main circuit main
module main (
  input  [1:0] A,
  input  [1:0] B,
  output [3:0] M
);

  wire and_1_out, and_2_out, and_3_out, and_4_out, and_5_out, and_6_out, and_7_out, and_8_out, and_9_out;

  and and_1 (and_1_out, A[1], B[1]);
  and and_2 (and_2_out, A[1], B[0]);
  and and_3 (and_3_out, A[0], B[1]);
  and and_4 (and_4_out, A[1], B[0]);
  and and_5 (and_5_out, A[1], B[1]);
  and and_6 (and_6_out, A[0], B[1]);
  and and_7 (and_7_out, A[1], B[0]);
  and and_8 (and_8_out, A[1], B[1]);
  and M0 (M[0], A[0], B[0]);
  and and_9 (and_9_out, and_3_out, and_4_out);
  xor M1 (M[1], and_1_out, and_2_out);
  xor M2 (M[2], and_9_out, and_5_out);
  and M3 (M[3], and_6_out, and_7_out, and_8_out);
endmodule
