// Logisim project Lab3_Ex3.circ as structural Verilog: 3 circuits, main circuit main
module main (
  input  [2:0] A,
  input  [1:0] B,
  output [4:0] Output
);

  wire A0B1_out, A1B0_out, A1B1_out, A2B0_out, A2B1_out, Full_Bit_Adder_c_out, Half_Bit_Adder_out_4;

  and A0B0 (Output[0], A[0], B[0]);
  and A1B0 (A1B0_out, A[1], B[0]);
  and A0B1 (A0B1_out, A[0], B[1]);
  and A2B0 (A2B0_out, A[2], B[0]);
  and A1B1 (A1B1_out, A[1], B[1]);
  and A2B1 (A2B1_out, A[2], B[1]);
  Half_Bit_Adder Half_Bit_Adder (.in_1(A1B0_out), .in_2(A0B1_out), .out_3(Output[1]), .out_4(Half_Bit_Adder_out_4));
  Full_Bit_Adder Full_Bit_Adder (
    .a(A2B0_out), .b(A1B1_out), .c_in(Half_Bit_Adder_out_4), .sum(Output[2]), .c_out(Full_Bit_Adder_c_out));
  Half_Bit_Adder Half_Bit_Adder_2 (.in_1(A2B1_out), .in_2(Full_Bit_Adder_c_out), .out_3(Output[3]), .out_4(Output[4]));
endmodule

module Full_Bit_Adder (
  input  a,
  input  b,
  input  c_in,
  output sum,
  output c_out
);

  wire and_1_out, and_2_out, xor_1_out;

  xor xor_1 (xor_1_out, a, b);
  and and_1 (and_1_out, b, a);
  xor xor_2 (sum, xor_1_out, c_in);
  and and_2 (and_2_out, c_in, xor_1_out);
  or or_1 (c_out, and_2_out, and_1_out);

  // Notes on the sheet:
  //   1 - Bit full adder
endmodule

module Half_Bit_Adder (
  input  in_1,
  input  in_2,
  output out_3,
  output out_4
);

  xor xor_1 (out_3, in_1, in_2);
  and and_1 (out_4, in_2, in_1);

  // Notes on the sheet:
  //   1-bit half adder
endmodule
