// Logisim project Lab5_Ex1.circ as structural Verilog: 4 circuits, main circuit main
module main (
  input  [3:0] A,
  input  [3:0] B,
  input  [1:0] S1_S0,
  input  S2,
  output [3:0] F,
  output Neg
);

  wire A___1_c, A___1_v, A___B_2_c, A___B_2_v, A___B_c, A___B_v, B___A_c, B___A_v, multiplexer_3_out,
       multiplexer_4_out, n7_segment_display_1_sa, n7_segment_display_1_sb, n7_segment_display_1_sc,
       n7_segment_display_1_sd, n7_segment_display_1_se, n7_segment_display_1_sf, n7_segment_display_1_sg;
  wire [2:0] multiplexer_5_out;
  wire [3:0] A___1_s, A___B_2_s, A___B_s, and_1_out, B___A_s, demultiplexer_1_out0, demultiplexer_1_out1,
       multiplexer_1_out, multiplexer_2_out, n4_bit_adder_subtracter_1_s, not_1_out, or_1_out, xnor_1_out,
       xor_1_out;

  _4_bit_adder_subtracter A___1 (.B(4'b0001), .A(A), .C(A___1_c), .V(A___1_v), .M(1'b0), .S(A___1_s));
  _4_bit_adder_subtracter A___B (.B(B), .A(A), .C(A___B_c), .V(A___B_v), .M(1'b0), .S(A___B_s));
  _4_bit_adder_subtracter A___B_2 (.B(B), .A(A), .C(A___B_2_c), .V(A___B_2_v), .M(1'b1), .S(A___B_2_s));
  _4_bit_adder_subtracter B___A (.B(A), .A(B), .C(B___A_c), .V(B___A_v), .M(1'b1), .S(B___A_s));
  assign and_1_out = A & B;  // AND_Gate and_1, 4 bits wide
  assign or_1_out = A | B;  // OR_Gate or_1, 4 bits wide
  assign xor_1_out = A ^ B;  // XOR_Gate xor_1, 4 bits wide
  assign xnor_1_out = ~(A ^ B);  // XNOR_Gate xnor_1, 4 bits wide
  Multiplexer #(.select(2), .width(4), .enable("false")) multiplexer_1 (
    .in0(and_1_out), .in1(or_1_out), .in2(xor_1_out), .in3(xnor_1_out), .out(multiplexer_1_out), .sel(S1_S0));
  Multiplexer #(.select(2), .width(4), .enable("false")) multiplexer_2 (
    .in0(A___1_s), .in1(A___B_s), .in2(A___B_2_s), .in3(B___A_s), .out(multiplexer_2_out), .sel(S1_S0));
  Multiplexer #(.select(2), .enable("false")) multiplexer_3 (
    .in0(A___1_c), .in1(A___B_c), .in2(A___B_2_c), .in3(B___A_c), .out(multiplexer_3_out), .sel(S1_S0));
  Multiplexer #(.select(2), .enable("false")) multiplexer_4 (
    .in0(A___1_v), .in1(A___B_v), .in2(A___B_2_v), .in3(B___A_v), .out(multiplexer_4_out), .sel(S1_S0));
  Multiplexer #(.width(4), .enable("false")) multiplexer_5 (
    .in0(multiplexer_1_out), .in1(multiplexer_2_out), .out({Neg, multiplexer_5_out}), .sel(S2));
  assign not_1_out = ~{Neg, multiplexer_5_out};  // NOT_Gate not_1, 4 bits wide
  LED C (.in(multiplexer_3_out));
  LED V (.in(multiplexer_4_out));
  _4_bit_adder_subtracter u_4_bit_adder_subtracter_1 (
    .B(4'b0001), .A(not_1_out), .M(1'b0), .S(n4_bit_adder_subtracter_1_s));  // open: C, V
  Multiplexer #(.width(4), .enable("false")) multiplexer_6 (
    .in0({Neg, multiplexer_5_out}), .in1(n4_bit_adder_subtracter_1_s), .out(F), .sel(Neg));
  Demultiplexer #(.width(4), .enable("false")) demultiplexer_1 (
    .out0(demultiplexer_1_out0), .out1(demultiplexer_1_out1), .in(F), .sel(S2));
  _7_Segment_Display u_7_segment_display_1 (
    .D(demultiplexer_1_out1), .Sa(n7_segment_display_1_sa), .Sb(n7_segment_display_1_sb),
    .Sc(n7_segment_display_1_sc), .Sd(n7_segment_display_1_sd), .Se(n7_segment_display_1_se),
    .Sf(n7_segment_display_1_sf), .Sg(n7_segment_display_1_sg));
  LED LED___8 (.in(multiplexer_1_out[0]));
  LED LED___4 (.in(multiplexer_1_out[1]));
  LED LED___2 (.in(multiplexer_1_out[2]));
  LED LED___1 (.in(multiplexer_1_out[3]));
  _7_Segment_Display_part u_7_segment_display_2 (
    .g(n7_segment_display_1_sg), .f(n7_segment_display_1_sf), .a(n7_segment_display_1_sa),
    .b(n7_segment_display_1_sb), .e(n7_segment_display_1_se), .d(n7_segment_display_1_sd),
    .c(n7_segment_display_1_sc));  // open: dp
endmodule

module _7_Segment_Display (
  input  [3:0] D,
  output Sa,
  output Sb,
  output Sc,
  output Sd,
  output Se,
  output Sf,
  output Sg
);

  wire and_1_out, and_2_out, and_3_out, and_4_out, and_5_out, and_6_out, and_7_out, and_8_out, and_9_out,
       and_10_out, and_11_out, and_12_out, and_13_out, and_14_out, and_15_out, and_16_out, not_1_out,
       not_2_out, not_3_out, not_4_out, not_5_out, not_6_out, not_7_out, not_8_out, not_9_out, not_10_out,
       not_11_out, not_12_out, not_13_out, not_14_out, not_15_out, not_16_out, not_17_out, not_18_out,
       not_19_out, not_20_out, not_21_out;

  not not_1 (not_1_out, D[2]);
  not not_2 (not_2_out, D[0]);
  not not_3 (not_3_out, D[1]);
  not not_4 (not_4_out, D[0]);
  not not_5 (not_5_out, D[1]);
  not not_6 (not_6_out, D[2]);
  not not_7 (not_7_out, D[0]);
  not not_8 (not_8_out, D[2]);
  not not_9 (not_9_out, D[0]);
  not not_10 (not_10_out, D[1]);
  not not_11 (not_11_out, D[2]);
  not not_12 (not_12_out, D[0]);
  not not_13 (not_13_out, D[0]);
  not not_14 (not_14_out, D[1]);
  not not_15 (not_15_out, D[0]);
  not not_16 (not_16_out, D[1]);
  not not_17 (not_17_out, D[0]);
  not not_18 (not_18_out, D[2]);
  not not_19 (not_19_out, D[1]);
  not not_20 (not_20_out, D[0]);
  and and_1 (and_1_out, not_1_out, not_2_out);
  and and_2 (and_2_out, D[2], D[0]);
  not not_21 (not_21_out, D[2]);
  and and_3 (and_3_out, not_3_out, not_4_out);
  and and_4 (and_4_out, D[1], D[0]);
  or or_1 (Sc, not_5_out, D[0], D[2]);
  and and_5 (and_5_out, not_6_out, not_7_out);
  and and_6 (and_6_out, not_8_out, D[1]);
  and and_7 (and_7_out, D[1], not_9_out);
  and and_8 (and_8_out, D[2], not_10_out, D[0]);
  and and_9 (and_9_out, not_11_out, not_12_out);
  and and_10 (and_10_out, D[1], not_13_out);
  and and_11 (and_11_out, not_14_out, not_15_out);
  and and_12 (and_12_out, D[2], not_16_out);
  and and_13 (and_13_out, D[2], not_17_out);
  and and_14 (and_14_out, not_18_out, D[1]);
  and and_15 (and_15_out, D[2], not_19_out);
  and and_16 (and_16_out, D[2], not_20_out);
  or or_2 (Sa, and_1_out, D[1], and_2_out, D[3]);
  or or_3 (Sb, not_21_out, and_3_out, and_4_out);
  or or_4 (Sd, and_5_out, and_6_out, and_7_out, and_8_out, D[3]);
  or or_5 (Se, and_9_out, and_10_out);
  or or_6 (Sf, and_11_out, and_12_out, and_13_out, D[3]);
  or or_7 (Sg, and_14_out, and_15_out, and_16_out, D[3]);
  _7_Segment_Display_part u_7_segment_display_1 (.g(Sg), .f(Sf), .a(Sa), .b(Sb), .e(Se), .d(Sd), .c(Sc));  // open: dp
endmodule

module _1_bit_Full_Adder (
  input  a,
  input  b,
  input  c_in,
  output sum,
  output c_out
);

  wire and_1_out, and_2_out, xor_1_out;

  xor xor_1 (xor_1_out, a, b);
  and and_1 (and_1_out, b, a);
  xor xor_2 (sum, xor_1_out, c_in);
  and and_2 (and_2_out, c_in, xor_1_out);
  or or_1 (c_out, and_2_out, and_1_out);

  // Notes on the sheet:
  //   1 - Bit full adder
endmodule

module _4_bit_adder_subtracter (
  input  [3:0] B,
  input  [3:0] A,
  input  M,
  output C,
  output V,
  output [3:0] S
);

  wire n1_bit_full_adder_2_c_out, n1_bit_full_adder_3_c_out, n1_bit_full_adder_4_c_out, xor_2_out, xor_3_out,
       xor_4_out, xor_5_out;

  xor xor_1 (V, C, n1_bit_full_adder_2_c_out);
  xor xor_2 (xor_2_out, B[3], M);
  _1_bit_Full_Adder u_1_bit_full_adder_1 (
    .a(A[3]), .b(xor_2_out), .c_in(n1_bit_full_adder_2_c_out), .sum(S[3]), .c_out(C));
  xor xor_3 (xor_3_out, B[2], M);
  _1_bit_Full_Adder u_1_bit_full_adder_2 (
    .a(A[2]), .b(xor_3_out), .c_in(n1_bit_full_adder_3_c_out), .sum(S[2]), .c_out(n1_bit_full_adder_2_c_out));
  xor xor_4 (xor_4_out, B[1], M);
  _1_bit_Full_Adder u_1_bit_full_adder_3 (
    .a(A[1]), .b(xor_4_out), .c_in(n1_bit_full_adder_4_c_out), .sum(S[1]), .c_out(n1_bit_full_adder_3_c_out));
  xor xor_5 (xor_5_out, B[0], M);
  _1_bit_Full_Adder u_1_bit_full_adder_4 (
    .a(A[0]), .b(xor_5_out), .c_in(M), .sum(S[0]), .c_out(n1_bit_full_adder_4_c_out));
endmodule
