// Logisim project Lab6_Ex1.circ as structural Verilog: 2 circuits, main circuit main
module main (
  output A,
  output B,
  output C
);

  wire and_1_out, and_2_out, and_3_out, and_4_out, and_5_out, clock_1_out, d_ff_1_qn, d_ff_2_qn, d_ff_3_qn,
       n7_segment_display_1_sa, n7_segment_display_1_sb, n7_segment_display_1_sc, n7_segment_display_1_sd,
       n7_segment_display_1_se, n7_segment_display_1_sf, n7_segment_display_1_sg, or_1_out, or_2_out,
       or_3_out;

  and and_1 (and_1_out, d_ff_2_qn, d_ff_3_qn);
  and and_2 (and_2_out, B, C);
  and and_3 (and_3_out, d_ff_1_qn, d_ff_2_qn);
  and and_4 (and_4_out, B, d_ff_3_qn);
  and and_5 (and_5_out, d_ff_1_qn, d_ff_3_qn);
  or or_1 (or_1_out, and_1_out, and_2_out);
  or or_2 (or_2_out, and_3_out, and_4_out);
  or or_3 (or_3_out, and_5_out, A);
  Clock #(.lowDuration(2)) clock_1 (.out(clock_1_out));
  D_Flip_Flop d_ff_1 (.clk(clock_1_out), .D(or_1_out), .Q(A), .Qn(d_ff_1_qn));  // open: preset, en, reset
  D_Flip_Flop d_ff_2 (.clk(clock_1_out), .D(or_2_out), .Q(B), .Qn(d_ff_2_qn));  // open: preset, en, reset
  D_Flip_Flop d_ff_3 (.clk(clock_1_out), .D(or_3_out), .Q(C), .Qn(d_ff_3_qn));  // open: preset, en, reset
  _7_Segment_Display u_7_segment_display_1 (
    .D3(1'b0), .D2(A), .D1(B), .D0(C), .Sa(n7_segment_display_1_sa), .Sb(n7_segment_display_1_sb),
    .Sc(n7_segment_display_1_sc), .Sd(n7_segment_display_1_sd), .Se(n7_segment_display_1_se),
    .Sf(n7_segment_display_1_sf), .Sg(n7_segment_display_1_sg));
  _7_Segment_Display_part u_7_segment_display_2 (
    .g(n7_segment_display_1_sg), .f(n7_segment_display_1_sf), .a(n7_segment_display_1_sa),
    .b(n7_segment_display_1_sb), .e(n7_segment_display_1_se), .d(n7_segment_display_1_sd),
    .c(n7_segment_display_1_sc));  // open: dp

  // Notes on the sheet:
  //   C'
  //   B
  //   C
  //   B'
  //   A'
  //   A
  //   B'C' + BC
  //   A'B' + BC'
  //   A'C' + A
endmodule

module _7_Segment_Display (
  input  D3,
  input  D2,
  input  D1,
  input  D0,
  output Sa,
  output Sb,
  output Sc,
  output Sd,
  output Se,
  output Sf,
  output Sg
);

  wire and_1_out, and_2_out, and_3_out, and_4_out, and_5_out, and_6_out, and_7_out, and_8_out, and_9_out,
       and_10_out, and_11_out, and_12_out, and_13_out, and_14_out, and_15_out, and_16_out, not_1_out,
       not_2_out, not_3_out, not_4_out, not_5_out, not_6_out, not_7_out, not_8_out, not_9_out, not_10_out,
       not_11_out, not_12_out, not_13_out, not_14_out, not_15_out, not_16_out, not_17_out, not_18_out,
       not_19_out, not_20_out, not_21_out;

  not not_1 (not_1_out, D2);
  not not_2 (not_2_out, D0);
  not not_3 (not_3_out, D1);
  not not_4 (not_4_out, D0);
  not not_5 (not_5_out, D1);
  not not_6 (not_6_out, D2);
  not not_7 (not_7_out, D0);
  not not_8 (not_8_out, D2);
  not not_9 (not_9_out, D0);
  not not_10 (not_10_out, D1);
  not not_11 (not_11_out, D2);
  not not_12 (not_12_out, D0);
  not not_13 (not_13_out, D0);
  not not_14 (not_14_out, D1);
  not not_15 (not_15_out, D0);
  not not_16 (not_16_out, D1);
  not not_17 (not_17_out, D0);
  not not_18 (not_18_out, D2);
  not not_19 (not_19_out, D1);
  not not_20 (not_20_out, D0);
  and and_1 (and_1_out, not_1_out, not_2_out);
  and and_2 (and_2_out, D2, D0);
  not not_21 (not_21_out, D2);
  and and_3 (and_3_out, not_3_out, not_4_out);
  and and_4 (and_4_out, D1, D0);
  or or_1 (Sc, not_5_out, D0, D2);
  and and_5 (and_5_out, not_6_out, not_7_out);
  and and_6 (and_6_out, not_8_out, D1);
  and and_7 (and_7_out, D1, not_9_out);
  and and_8 (and_8_out, D2, not_10_out, D0);
  and and_9 (and_9_out, not_11_out, not_12_out);
  and and_10 (and_10_out, D1, not_13_out);
  and and_11 (and_11_out, not_14_out, not_15_out);
  and and_12 (and_12_out, D2, not_16_out);
  and and_13 (and_13_out, D2, not_17_out);
  and and_14 (and_14_out, not_18_out, D1);
  and and_15 (and_15_out, D2, not_19_out);
  and and_16 (and_16_out, D2, not_20_out);
  or or_2 (Sa, and_1_out, D1, and_2_out, D3);
  or or_3 (Sb, not_21_out, and_3_out, and_4_out);
  or or_4 (Sd, and_5_out, and_6_out, and_7_out, and_8_out, D3);
  or or_5 (Se, and_9_out, and_10_out);
  or or_6 (Sf, and_11_out, and_12_out, and_13_out, D3);
  or or_7 (Sg, and_14_out, and_15_out, and_16_out, D3);
  _7_Segment_Display_part u_7_segment_display_1 (.g(Sg), .f(Sf), .a(Sa), .b(Sb), .e(Se), .d(Sd), .c(Sc));  // open: dp
endmodule
